// Logisim project 7lista.circ as structural Verilog: 2 circuits, main circuit circuito_teste
module circuito_teste (
  input  A,
  input  B,
  input  C,
  input  D,
  output Z
);

  wire and_1_out, and_2_out, and_3_out, nand_1_out, not_1_out, not_2_out, not_3_out, not_4_out;

  not not_1 (not_1_out, A);
  not not_2 (not_2_out, B);
  not not_3 (not_3_out, C);
  not not_4 (not_4_out, D);
  nand nand_1 (nand_1_out, not_1_out, B, D);
  and and_1 (and_1_out, not_1_out, C, nand_1_out);
  and and_2 (and_2_out, not_1_out, B, not_3_out, not_4_out);
  and and_3 (and_3_out, A, not_2_out, C);
  or or_1 (Z, and_1_out, and_2_out, and_3_out);
endmodule

module c2 (
  input  A,
  input  B,
  input  C,
  input  D,
  output Z
);

  wire and_1_out, and_2_out, and_3_out, nand_1_out, not_1_out, not_2_out, not_3_out, not_4_out;

  not not_1 (not_1_out, A);
  not not_2 (not_2_out, B);
  not not_3 (not_3_out, C);
  not not_4 (not_4_out, D);
  nand nand_1 (nand_1_out, not_1_out, B, D);
  and and_1 (and_1_out, not_1_out, C, nand_1_out);
  and and_2 (and_2_out, not_1_out, B, not_3_out, not_4_out);
  and and_3 (and_3_out, A, not_2_out, C);
  or or_1 (Z, and_1_out, and_2_out, and_3_out);
endmodule
