// Logisim project MAR_SAP1.circ as structural Verilog: 1 circuit, main circuit MAR
module MAR (
  input  in_1,
  input  in_2,
  input  in_3,
  input  nLm,
  input  in_5,
  input  CLK,
  input  vem_da_RAM__CE,
  output indicador_de_atividade,
  output out_9,
  output out_10,
  output out_11,
  output out_12
);

  wire not_1_out;

  or or_1 (indicador_de_atividade, not_1_out, vem_da_RAM__CE);
  not not_1 (not_1_out, nLm);
  Register #(.width(4)) register_1 (
    .D({in_1, in_2, in_3, in_5}), .en(not_1_out), .Q({out_9, out_10, out_11, out_12}), .clk(CLK));  // open: clr
endmodule
