// Logisim project RAM_SAP1.circ as structural Verilog: 1 circuit, main circuit RAM 16 X 8
module RAM_16_X_8 (
  input  in_1,
  input  Addr__from_PC,
  input  in_3,
  input  in_4,
  input  CE,
  input  WE,
  input  Run_1__Prog_0,
  input  in_8,
  input  [3:0] in_9,
  input  [7:0] in_10,
  output out_11,
  output out_12,
  output out_13,
  output out_14,
  output out_15,
  output out_16,
  output out_17,
  output out_18,
  output out_19,
  output mostrador_de_atividade
);

  wire not_1_out;
  wire [3:0] multiplexer_1_out;
  wire [7:0] ram_1_data;

  Multiplexer #(.width(4), .enable("false")) multiplexer_1 (
    .in0(in_9), .in1({in_1, Addr__from_PC, in_3, in_4}), .out(multiplexer_1_out), .sel(Run_1__Prog_0));
  not not_1 (not_1_out, Run_1__Prog_0);
  RAM #(.addrWidth(4), .bus("separate")) ram_1 (
    .addr(multiplexer_1_out), .din(in_10), .data(ram_1_data), .str(not_1_out), .sel(1'b1), .clk(WE),
    .ld(Run_1__Prog_0), .clr(in_8));
  assign {out_19, out_18, out_17, out_16, out_15, out_14, out_12, out_11} = mostrador_de_atividade ? ram_1_data : 8'bz;  // Controlled_Buffer controlled_buffer_1
  not not_2 (mostrador_de_atividade, CE);

  assign out_13 = mostrador_de_atividade;

  // Other names for the same wires on the sheet: Addr[3:0] = in_9

  // Notes on the sheet:
  //   Input Contents
  //   Clear Memory Contents
endmodule
