// Logisim project RI_SAP1.circ as structural Verilog: 1 circuit, main circuit RI
module RI (
  input  in_1,
  input  in_2,
  input  in_3,
  input  Li,
  input  in_5,
  input  CLK,
  input  in_7,
  input  CLR,
  input  in_9,
  input  in_10,
  input  in_11,
  input  Ei,
  input  in_13,
  output out_14,
  output out_15,
  output out_16,
  output out_17,
  output out_18,
  output out_19,
  output out_20,
  output out_21,
  output out_22
);

  wire not_1_out, not_2_out, xor_1_out;
  wire [3:0] register_2_q;

  or or_1 (out_14, xor_1_out, in_13);
  xor xor_1 (xor_1_out, not_2_out, not_1_out);
  not not_1 (not_1_out, Li);
  not not_2 (not_2_out, Ei);
  Register #(.width(4)) register_1 (
    .D({in_1, in_2, in_3, in_5}), .en(not_1_out), .Q({out_15, out_16, out_17, out_18}), .clk(CLK), .clr(CLR));
  Register #(.width(4)) register_2 (
    .D({in_7, in_9, in_10, in_11}), .en(not_1_out), .Q(register_2_q), .clk(CLK), .clr(CLR));
  assign {out_22, out_21, out_20, out_19} = not_2_out ? register_2_q : 4'bz;  // Controlled_Buffer controlled_buffer_1
endmodule
