// Logisim project RegistradorB_SAP1.circ as structural Verilog: 1 circuit, main circuit REG_B
module REG_B (
  input  in_1,
  input  in_2,
  input  in_3,
  input  in_4,
  input  in_5,
  input  in_6,
  input  in_7,
  input  in_8,
  input  in_9,
  input  in_10,
  input  vem_da_ULA__Eu,
  output out_12,
  output out_13,
  output out_14,
  output out_15,
  output out_16,
  output out_17,
  output out_18,
  output out_19,
  output indicador_de_atividade
);

  wire Lb;

  Register #(.width(4)) register_1 (
    .D({in_8, in_7, in_6, in_5}), .en(Lb), .Q({out_12, out_13, out_14, out_15}), .clk(in_10));  // open: clr
  Register #(.width(4)) register_2 (
    .D({in_4, in_3, in_2, in_1}), .en(Lb), .Q({out_16, out_17, out_18, out_19}), .clk(in_10));  // open: clr
  not not_1 (Lb, in_9);
  or or_1 (indicador_de_atividade, Lb, vem_da_ULA__Eu);

  // Other names for the same wires on the sheet: CLK = in_10
endmodule
