// Logisim project contador_2bits_assincrono.circ as structural Verilog: 1 circuit, main circuit main
module main (
  input  T,
  input  Clk,
  output out_3,
  output bMs
);

  T_Flip_Flop #(.trigger("falling")) t_ff_1 (.T(T), .clk(Clk), .Q(out_3));  // open: Qn, reset, preset
  T_Flip_Flop #(.trigger("falling")) t_ff_2 (.T(T), .clk(out_3), .Q(bMs));  // open: Qn, reset, preset
endmodule
