// Logisim project contador_2bits_sincrono.circ as structural Verilog: 5 circuits, main circuit main
module main (
  input  q0,
  input  q1,
  input  q2,
  input  q3,
  input  clk,
  output [3:0] out_6
);

  wire and_1_out, and_2_out, and_3_out, and_4_out, and_5_out, or_1_out, or_2_out;

  D_Flip_Flop D0 (.D(and_1_out), .clk(clk), .Q(out_6[3]));  // open: Qn, preset, reset
  and and_1 (and_1_out, ~q0, ~q1, ~q2, ~q3);  // AND_Gate
  and and_2 (and_2_out, ~q0, q1, q2, ~q3);  // AND_Gate
  and and_3 (and_3_out, q0, ~q1, ~q2, ~q3);  // AND_Gate
  D_Flip_Flop D1 (.D(or_1_out), .clk(clk), .Q(out_6[2]));  // open: Qn, preset, reset
  or or_1 (or_1_out, and_2_out, and_3_out);
  and and_4 (and_4_out, ~q0, q1, ~q2, ~q3);  // AND_Gate
  and and_5 (and_5_out, q0, ~q1, ~q2, ~q3);  // AND_Gate
  D_Flip_Flop D2 (.D(or_2_out), .clk(clk), .Q(out_6[1]));  // open: Qn, preset, reset
  or or_2 (or_2_out, and_4_out, and_5_out);
  D_Flip_Flop D4 (.D(1'b0), .clk(clk), .Q(out_6[0]));  // open: Qn, preset, reset
endmodule

module Q0_circ (
  input  q0,
  input  q1,
  input  q2,
  input  q3,
  output d0
);

  and and_1 (d0, ~q0, ~q1, ~q2, ~q3);  // AND_Gate
endmodule

module Q1_circ (
  input  q0,
  input  q1,
  input  q2,
  input  q3,
  output d1
);

  wire and_1_out, and_2_out;

  and and_1 (and_1_out, ~q0, q1, q2, ~q3);  // AND_Gate
  and and_2 (and_2_out, q0, ~q1, ~q2, ~q3);  // AND_Gate
  or or_1 (d1, and_1_out, and_2_out);
endmodule

module Q2_circ (
  input  q0,
  input  q1,
  input  q2,
  input  q3,
  output d2
);

  wire and_1_out, and_2_out;

  and and_1 (and_1_out, ~q0, q1, ~q2, ~q3);  // AND_Gate
  and and_2 (and_2_out, q0, ~q1, ~q2, ~q3);  // AND_Gate
  or or_1 (d2, and_1_out, and_2_out);
endmodule

module copia (
  input  clk,
  output [3:0] out_2
);

  wire clock_1_out, q0_circ_1_d0, q1_circ_1_d1, q2_circ_1_d2, undriven;

  // NoConnect on clk
  Clock clock_1 (.out(clock_1_out));
  D_Flip_Flop D0 (.D(q0_circ_1_d0), .clk(clock_1_out), .Q(out_2[3]));  // open: Qn, preset, reset
  Q0_circ q0_circ_1 (.q0(out_2[3]), .q1(out_2[2]), .q2(out_2[1]), .q3(out_2[0]), .d0(q0_circ_1_d0));
  Q1_circ q1_circ_1 (.q0(out_2[3]), .q1(out_2[2]), .q2(out_2[1]), .q3(out_2[0]), .d1(q1_circ_1_d1));
  D_Flip_Flop D1 (.D(q1_circ_1_d1), .clk(clock_1_out), .Q(out_2[2]), .preset(undriven));  // open: Qn, reset
  Hex_Digit_Display hex_digit_display_1 (.value(out_2));  // open: dp
  Q2_circ q2_circ_1 (.q0(out_2[3]), .q1(out_2[2]), .q2(out_2[1]), .q3(out_2[0]), .d2(q2_circ_1_d2));
  D_Flip_Flop D2 (.D(q2_circ_1_d2), .clk(clock_1_out), .Q(out_2[1]));  // open: Qn, preset, reset
  D_Flip_Flop D4 (.D(1'b0), .clk(clock_1_out), .Q(out_2[0]));  // open: Qn, preset, reset

  // Other names for the same wires on the sheet: q3 = out_2[0]; q2 = out_2[1]; q1 = out_2[2]; q0 = out_2[3]
endmodule
