// Logisim project contador_anel_jhonson_2sentidos.circ as structural Verilog: 1 circuit, main circuit main
module main (
  input  in_1,
  input  in_2,
  input  in_3,
  input  in_4,
  input  in_5,
  input  in_6,
  input  in_7,
  input  in_8
);

  wire clock_1_out, clock_2_out, clock_3_out, clock_4_out, controlled_buffer_1_out, controlled_buffer_2_out,
       controlled_buffer_3_out, controlled_buffer_4_out, j_k_ff_1_q, j_k_ff_1_qn, j_k_ff_2_q, j_k_ff_2_qn,
       j_k_ff_3_q, j_k_ff_3_qn, j_k_ff_4_q, j_k_ff_4_qn, j_k_ff_5_q, j_k_ff_5_qn, j_k_ff_6_q, j_k_ff_6_qn,
       j_k_ff_7_q, j_k_ff_7_qn, j_k_ff_8_q, j_k_ff_8_qn, j_k_ff_9_q, j_k_ff_9_qn, j_k_ff_10_q, j_k_ff_10_qn,
       j_k_ff_11_q, j_k_ff_11_qn, j_k_ff_12_q, j_k_ff_12_qn, j_k_ff_13_q, j_k_ff_13_qn, j_k_ff_14_q,
       j_k_ff_14_qn, j_k_ff_15_q, j_k_ff_15_qn, j_k_ff_16_q, j_k_ff_16_qn;

  Clock clock_1 (.out(clock_1_out));
  Clock clock_2 (.out(clock_2_out));
  assign controlled_buffer_1_out = in_4 ? in_2 : 1'bz;  // Controlled_Buffer controlled_buffer_1
  assign controlled_buffer_2_out = in_8 ? in_6 : 1'bz;  // Controlled_Buffer controlled_buffer_2
  LED led_1 (.in(j_k_ff_1_q));
  J_K_Flip_Flop j_k_ff_1 (
    .J(j_k_ff_3_q), .clk(clock_1_out), .K(j_k_ff_3_qn), .Q(j_k_ff_1_q), .Qn(j_k_ff_1_qn),
    .reset(controlled_buffer_1_out));  // open: preset, en
  LED led_2 (.in(j_k_ff_2_q));
  J_K_Flip_Flop j_k_ff_2 (
    .J(j_k_ff_4_q), .clk(clock_2_out), .K(j_k_ff_4_qn), .Q(j_k_ff_2_q), .Qn(j_k_ff_2_qn),
    .reset(controlled_buffer_2_out));  // open: preset, en
  LED led_3 (.in(j_k_ff_3_q));
  J_K_Flip_Flop j_k_ff_3 (
    .J(j_k_ff_5_q), .clk(clock_1_out), .K(j_k_ff_5_qn), .Q(j_k_ff_3_q), .Qn(j_k_ff_3_qn),
    .reset(controlled_buffer_1_out));  // open: preset, en
  LED led_4 (.in(j_k_ff_4_q));
  J_K_Flip_Flop j_k_ff_4 (
    .J(j_k_ff_6_q), .clk(clock_2_out), .K(j_k_ff_6_qn), .Q(j_k_ff_4_q), .Qn(j_k_ff_4_qn),
    .reset(controlled_buffer_2_out));  // open: preset, en
  J_K_Flip_Flop j_k_ff_5 (
    .J(j_k_ff_7_q), .clk(clock_1_out), .K(j_k_ff_7_qn), .Q(j_k_ff_5_q), .Qn(j_k_ff_5_qn),
    .reset(controlled_buffer_1_out));  // open: preset, en
  J_K_Flip_Flop j_k_ff_6 (
    .J(j_k_ff_8_q), .clk(clock_2_out), .K(j_k_ff_8_qn), .Q(j_k_ff_6_q), .Qn(j_k_ff_6_qn),
    .reset(controlled_buffer_2_out));  // open: preset, en
  LED led_5 (.in(j_k_ff_5_q));
  LED led_6 (.in(j_k_ff_6_q));
  LED led_7 (.in(j_k_ff_7_q));
  J_K_Flip_Flop j_k_ff_7 (
    .J(j_k_ff_1_q), .clk(clock_1_out), .K(j_k_ff_1_qn), .Q(j_k_ff_7_q), .Qn(j_k_ff_7_qn),
    .preset(controlled_buffer_1_out));  // open: en, reset
  LED led_8 (.in(j_k_ff_8_q));
  J_K_Flip_Flop j_k_ff_8 (
    .J(j_k_ff_2_qn), .clk(clock_2_out), .K(j_k_ff_2_q), .Q(j_k_ff_8_q), .Qn(j_k_ff_8_qn),
    .preset(controlled_buffer_2_out));  // open: en, reset
  Clock clock_3 (.out(clock_3_out));
  assign controlled_buffer_3_out = in_3 ? in_1 : 1'bz;  // Controlled_Buffer controlled_buffer_3
  Clock clock_4 (.out(clock_4_out));
  assign controlled_buffer_4_out = in_7 ? in_5 : 1'bz;  // Controlled_Buffer controlled_buffer_4
  LED led_9 (.in(j_k_ff_9_q));
  J_K_Flip_Flop j_k_ff_9 (
    .J(j_k_ff_14_q), .clk(clock_3_out), .K(j_k_ff_14_qn), .Q(j_k_ff_9_q), .Qn(j_k_ff_9_qn),
    .preset(controlled_buffer_3_out));  // open: en, reset
  J_K_Flip_Flop j_k_ff_10 (
    .J(j_k_ff_16_qn), .clk(clock_4_out), .K(j_k_ff_16_q), .Q(j_k_ff_10_q), .Qn(j_k_ff_10_qn),
    .preset(controlled_buffer_4_out));  // open: en, reset
  J_K_Flip_Flop j_k_ff_11 (
    .J(j_k_ff_9_q), .clk(clock_3_out), .K(j_k_ff_9_qn), .Q(j_k_ff_11_q), .Qn(j_k_ff_11_qn),
    .reset(controlled_buffer_3_out));  // open: preset, en
  LED led_10 (.in(j_k_ff_10_q));
  J_K_Flip_Flop j_k_ff_12 (
    .J(j_k_ff_10_q), .clk(clock_4_out), .K(j_k_ff_10_qn), .Q(j_k_ff_12_q), .Qn(j_k_ff_12_qn),
    .reset(controlled_buffer_4_out));  // open: preset, en
  LED led_11 (.in(j_k_ff_11_q));
  J_K_Flip_Flop j_k_ff_13 (
    .J(j_k_ff_11_q), .clk(clock_3_out), .K(j_k_ff_11_qn), .Q(j_k_ff_13_q), .Qn(j_k_ff_13_qn),
    .reset(controlled_buffer_3_out));  // open: preset, en
  LED led_12 (.in(j_k_ff_12_q));
  LED led_13 (.in(j_k_ff_13_q));
  J_K_Flip_Flop j_k_ff_14 (
    .J(j_k_ff_13_q), .clk(clock_3_out), .K(j_k_ff_13_qn), .Q(j_k_ff_14_q), .Qn(j_k_ff_14_qn),
    .reset(controlled_buffer_3_out));  // open: preset, en
  LED led_14 (.in(j_k_ff_15_q));
  J_K_Flip_Flop j_k_ff_15 (
    .J(j_k_ff_12_q), .clk(clock_4_out), .K(j_k_ff_12_qn), .Q(j_k_ff_15_q), .Qn(j_k_ff_15_qn),
    .reset(controlled_buffer_4_out));  // open: preset, en
  LED led_15 (.in(j_k_ff_14_q));
  LED led_16 (.in(j_k_ff_16_q));
  J_K_Flip_Flop j_k_ff_16 (
    .J(j_k_ff_15_q), .clk(clock_4_out), .K(j_k_ff_15_qn), .Q(j_k_ff_16_q), .Qn(j_k_ff_16_qn),
    .reset(controlled_buffer_4_out));  // open: preset, en

  // Notes on the sheet:
  //   Contador anel
  //   esquerda ← direita
  //   Contador jonhson
  //   esquerda ← direita
  //   Contador anel
  //   esquerda → direita
  //   Contador anel
  //   esquerda → direita
endmodule
