// Logisim project contador_decre.circ as structural Verilog: 1 circuit, main circuit main
module main (
  input  in_1,
  input  in_2,
  output [2:0] out_3,
  output [2:0] out_4
);

  wire clock_1_out, clock_2_out;

  Clock clock_1 (.out(clock_1_out));
  Clock clock_2 (.out(clock_2_out));
  T_Flip_Flop t_ff_1 (.T(in_1), .clk(clock_1_out), .Q(out_3[0]));  // open: Qn, reset, preset
  T_Flip_Flop #(.trigger("falling")) t_ff_2 (.T(in_2), .clk(clock_2_out), .Q(out_4[0]));  // open: Qn, reset, preset
  T_Flip_Flop t_ff_3 (.T(in_1), .clk(out_3[0]), .Q(out_3[1]));  // open: Qn, reset, preset
  T_Flip_Flop #(.trigger("falling")) t_ff_4 (.T(in_2), .clk(out_4[0]), .Q(out_4[1]));  // open: Qn, reset, preset
  T_Flip_Flop t_ff_5 (.T(in_1), .clk(out_3[1]), .Q(out_3[2]));  // open: Qn, reset, preset
  T_Flip_Flop #(.trigger("falling")) t_ff_6 (.T(in_2), .clk(out_4[1]), .Q(out_4[2]));  // open: Qn, reset, preset

  // Notes on the sheet:
  //   decescente
  //   crescente
endmodule
