// Logisim project contador_sin_JK_13578.circ as structural Verilog: 1 circuit, main circuit main
module main (
  output [3:0] out_1
);

  wire and_1_out, clock_1_out;

  Clock clock_1 (.out(clock_1_out));
  J_K_Flip_Flop #(.trigger("falling")) Q3 (
    .J(and_1_out), .K(1'b1), .clk(clock_1_out), .Q(out_1[3]));  // open: Qn, preset, reset
  and and_1 (and_1_out, out_1[1], out_1[2]);
  J_K_Flip_Flop #(.trigger("falling")) Q2 (
    .J(out_1[1]), .K(out_1[1]), .clk(clock_1_out), .Q(out_1[2]));  // open: Qn, preset, reset
  J_K_Flip_Flop #(.trigger("falling")) Q1 (
    .J(out_1[0]), .K(1'b1), .clk(clock_1_out), .Q(out_1[1]));  // open: Qn, preset, reset
  Hex_Digit_Display hex_digit_display_1 (.value(out_1));  // open: dp
  J_K_Flip_Flop #(.trigger("falling")) Q0 (
    .J(1'b1), .K(and_1_out), .clk(clock_1_out), .Q(out_1[0]));  // open: Qn, preset, reset
endmodule
