// Logisim project flip_flops.circ as structural Verilog: 5 circuits, main circuit main
module main (
  input  in_1,
  input  in_2,
  input  in_3,
  input  in_4,
  input  in_5,
  input  in_6,
  input  in_7,
  input  in_8,
  input  in_9,
  input  in_10,
  input  in_11,
  input  in_12,
  input  in_13,
  input  in_14
);

  wire clock_1_out, clock_2_out, clock_3_out, clock_4_out, d_ff_1_q, d_ff_1_qn, j_k_ff_1_q, j_k_ff_1_qn,
       s_r_ff_1_q, s_r_ff_1_qn, t_ff_1_q, t_ff_1_qn;

  Clock clock_1 (.out(clock_1_out));
  Clock clock_2 (.out(clock_2_out));
  D_Flip_Flop d_ff_1 (.D(in_3), .clk(clock_1_out), .Q(d_ff_1_q), .Qn(d_ff_1_qn), .preset(in_1), .reset(in_5));
  J_K_Flip_Flop j_k_ff_1 (
    .J(in_9), .K(in_11), .clk(clock_2_out), .Q(j_k_ff_1_q), .Qn(j_k_ff_1_qn), .preset(in_7), .reset(in_14));
  LED led_1 (.in(d_ff_1_q));
  LED led_2 (.in(d_ff_1_qn));
  LED led_3 (.in(j_k_ff_1_q));
  LED led_4 (.in(j_k_ff_1_qn));
  T_Flip_Flop t_ff_1 (.T(in_4), .clk(clock_3_out), .Q(t_ff_1_q), .Qn(t_ff_1_qn), .reset(in_6), .preset(in_2));
  Clock clock_3 (.out(clock_3_out));
  S_R_Flip_Flop s_r_ff_1 (
    .S(in_10), .R(in_12), .clk(clock_4_out), .Q(s_r_ff_1_q), .reset(in_13), .Qn(s_r_ff_1_qn), .preset(in_8));
  Clock clock_4 (.out(clock_4_out));
  LED led_5 (.in(t_ff_1_q));
  LED led_6 (.in(t_ff_1_qn));
  LED led_7 (.in(s_r_ff_1_q));
  LED led_8 (.in(s_r_ff_1_qn));
endmodule

module ff_D (
  input  in_1
);

  wire clock_1_out, d_ff_1_q, latch_d_1_q, latch_d_2_q, not_1_out;

  Clock clock_1 (.out(clock_1_out));
  D_Flip_Flop #(.trigger("falling")) d_ff_1 (.D(in_1), .clk(clock_1_out), .Q(d_ff_1_q));  // open: Qn, preset, reset
  LED led_1 (.in(d_ff_1_q));
  latch_D latch_d_1 (.D(in_1), .clk(clock_1_out), .Q(latch_d_1_q));
  not not_1 (not_1_out, clock_1_out);
  LED led_2 (.in(latch_d_2_q));
  latch_D latch_d_2 (.D(latch_d_1_q), .clk(not_1_out), .Q(latch_d_2_q));
endmodule

module latch_D (
  input  D,
  input  clk,
  output Q
);

  wire and_1_out, and_2_out, nor_1_out, not_1_out;

  not not_1 (not_1_out, D);
  and and_1 (and_1_out, D, clk);
  and and_2 (and_2_out, clk, not_1_out);
  nor nor_1 (nor_1_out, and_1_out, Q);
  nor nor_2 (Q, nor_1_out, and_2_out);

  // Notes on the sheet:
  //   S
  //   R
endmodule

module ff_JK (
  input  J,
  input  K,
  output Q,
  output NOT_Q
);

  wire and_1_out, and_2_out, clock_1_out, not_1_out, or_1_out;

  not not_1 (not_1_out, K);
  and and_1 (and_1_out, NOT_Q, J);
  and and_2 (and_2_out, not_1_out, Q);
  or or_1 (or_1_out, and_1_out, and_2_out);
  Clock clock_1 (.out(clock_1_out));
  D_Flip_Flop d_ff_1 (.D(or_1_out), .clk(clock_1_out), .Q(Q), .Qn(NOT_Q));  // open: preset, reset
endmodule

module ff_T (
  input  T,
  output out_2,
  output out_3
);

  ff_JK ff_jk_1 (.J(T), .K(T), .Q(out_2), .NOT_Q(out_3));
endmodule
