// Logisim project latch_D.circ as structural Verilog: 1 circuit, main circuit main
module main (
  input  D
);

  wire and_1_out, and_2_out, clock_1_out, nor_1_out, nor_2_out, not_1_out;

  Clock clock_1 (.out(clock_1_out));
  not not_1 (not_1_out, D);
  and and_1 (and_1_out, D, clock_1_out);
  and and_2 (and_2_out, clock_1_out, not_1_out);
  nor nor_1 (nor_1_out, and_1_out, nor_2_out);
  nor nor_2 (nor_2_out, nor_1_out, and_2_out);
  LED NOTQ (.in(nor_1_out));
  LED Q (.in(nor_2_out));

  // Notes on the sheet:
  //   S
  //   R
endmodule
