// Logisim project latch_JK.circ as structural Verilog: 1 circuit, main circuit main
module main (
  input  J,
  input  C,
  input  K
);

  wire and_1_out, and_2_out, nor_1_out, nor_2_out;

  and and_1 (and_1_out, nor_1_out, J, C);
  and and_2 (and_2_out, C, K, nor_2_out);
  nor nor_1 (nor_1_out, and_1_out, nor_2_out);
  nor nor_2 (nor_2_out, nor_1_out, and_2_out);
  LED Q (.in(nor_1_out));
  LED NOTQ (.in(nor_2_out));

  // Notes on the sheet:
  //   S
  //   R
endmodule
