// Logisim project latch_SR.circ as structural Verilog: 1 circuit, main circuit main
module main (
  input  S,
  input  R
);

  wire nand_1_out, nand_2_out, nor_1_out, nor_2_out, not_1_out, not_2_out;

  not not_1 (not_1_out, S);
  not not_2 (not_2_out, R);
  nor nor_1 (nor_1_out, S, nor_2_out);
  nor nor_2 (nor_2_out, nor_1_out, R);
  nand nand_1 (nand_1_out, not_1_out, nand_2_out);
  nand nand_2 (nand_2_out, nand_1_out, not_2_out);
  LED NOTQ (.in(nor_1_out));
  LED Q (.in(nor_2_out));
  LED NOT_Q (.in(nand_1_out));
  LED Q_1 (.in(nand_2_out));

  // Notes on the sheet:
  //   Usando portas NOR
  //   Usando portas NAND
endmodule
