// Logisim project latch_SR_sincrono.circ as structural Verilog: 1 circuit, main circuit main
module main (
  input  S,
  input  R
);

  wire and_1_out, and_2_out, and_3_out, and_4_out, CLK_out, clock_1_out, nand_1_out, nand_2_out, nor_1_out,
       nor_2_out, not_1_out, not_2_out;

  Clock CLK (.out(CLK_out));
  Clock clock_1 (.out(clock_1_out));
  and and_1 (and_1_out, S, CLK_out);
  and and_2 (and_2_out, CLK_out, R);
  and and_3 (and_3_out, S, clock_1_out);
  and and_4 (and_4_out, clock_1_out, R);
  not not_1 (not_1_out, and_3_out);
  not not_2 (not_2_out, and_4_out);
  nor nor_1 (nor_1_out, and_1_out, nor_2_out);
  nor nor_2 (nor_2_out, nor_1_out, and_2_out);
  LED NOTQ (.in(nor_1_out));
  LED Q (.in(nor_2_out));
  nand nand_1 (nand_1_out, not_1_out, nand_2_out);
  nand nand_2 (nand_2_out, nand_1_out, not_2_out);
  LED led_1 (.in(nand_1_out));
  LED led_2 (.in(nand_2_out));

  // Notes on the sheet:
  //   Usando portas NOR
  //   Usando postas NAND
endmodule
