// Logisim project lista.circ as structural Verilog: 3 circuits, main circuit main
module main (
  input  M,
  input  P4,
  input  P3,
  input  P2,
  input  P1,
  input  C0,
  input  C1,
  input  C2
);

  wire multiplexer_1_out;

  Multiplexer #(.select(3)) multiplexer_1 (
    .in0(M), .in1(P4), .in2(P3), .in3(P2), .in4(P1), .in5(1'b0), .in6(1'b0), .in7(1'b0),
    .out(multiplexer_1_out), .sel({C2, C1, C0}));
  LED led_1 (.in(multiplexer_1_out));
endmodule

module ANDs_ORs (
  input  M,
  input  P1,
  input  P2,
  input  P3,
  input  P4,
  input  C2,
  input  C1,
  input  C0
);

  wire and_1_out, and_2_out, and_3_out, and_4_out, and_5_out, or_1_out;

  and and_1 (and_1_out, M, ~C0, ~C1, ~C2);  // AND_Gate
  and and_2 (and_2_out, P1, C0, ~C1, ~C2);  // AND_Gate
  and and_3 (and_3_out, P2, ~C0, C1, ~C2);  // AND_Gate
  and and_4 (and_4_out, P3, C0, C1, ~C2);  // AND_Gate
  and and_5 (and_5_out, P4, ~C0, ~C1, C2);  // AND_Gate
  or or_1 (or_1_out, and_1_out, and_2_out, and_3_out, and_4_out, and_5_out);
  LED led_1 (.in(or_1_out));
endmodule

module circ2 (
  input  M,
  input  P1,
  input  P2,
  input  P3,
  input  P4,
  input  C2,
  input  C1,
  input  C0
);

  wire and_1_out, and_2_out, and_3_out, and_4_out, and_5_out, or_1_out;

  and and_1 (and_1_out, M, ~C0, ~C1, ~C2);  // AND_Gate
  and and_2 (and_2_out, P1, C0, ~C1, ~C2);  // AND_Gate
  and and_3 (and_3_out, P2, ~C0, C1, ~C2);  // AND_Gate
  and and_4 (and_4_out, P3, C0, C1, ~C2);  // AND_Gate
  and and_5 (and_5_out, P4, ~C0, ~C1, C2);  // AND_Gate
  or or_1 (or_1_out, and_1_out, and_2_out, and_3_out, and_4_out, and_5_out);
  LED led_1 (.in(or_1_out));
endmodule
