// Logisim project lista2unit.circ as structural Verilog: 2 circuits, main circuit main
module main (
  input  A,
  input  B,
  input  Ctrl,
  output Z
);

  wire and_1_out, and_2_out;

  and and_1 (and_1_out, A, Ctrl);
  and and_2 (and_2_out, B, ~Ctrl);  // AND_Gate
  or or_1 (Z, and_1_out, and_2_out);

  // Notes on the sheet:
  //   mux 2:1 com 1 bit
endmodule

module MUX_2_2BITS (
  input  D00,
  input  D10,
  input  D01,
  input  D11,
  input  S
);

  wire and_1_out, and_2_out, and_3_out, and_4_out, or_1_out, or_2_out;

  and and_1 (and_1_out, D00, S);
  and and_2 (and_2_out, D10, ~S);  // AND_Gate
  and and_3 (and_3_out, D01, S);
  and and_4 (and_4_out, D11, ~S);  // AND_Gate
  or or_1 (or_1_out, and_1_out, and_2_out);
  or or_2 (or_2_out, and_3_out, and_4_out);
  LED Y1 (.in(or_1_out));
  LED Y2 (.in(or_2_out));

  // Notes on the sheet:
  //   D0 = D00, D01
  //   D1 = D10, D11
endmodule
