// Logisim project Complemento_de_1_com_crtl.circ as structural Verilog: 1 circuit, main circuit main
module main (
  input  e3,
  input  e2,
  input  e1,
  input  e0,
  input  ctrl,
  output o3,
  output o2,
  output o1,
  output o0
);

  xor xor_1 (o3, ctrl, e3);
  xor xor_2 (o2, ctrl, e2);
  xor xor_3 (o1, ctrl, e1);
  xor xor_4 (o0, ctrl, e0);
endmodule
