// Logisim project Contador_ciclo_duplo_par_impar_3_bits.circ as structural Verilog: 1 circuit, main circuit main
module main (
  input  escreve_1,
  input  escreve_0,
  input  Carreg__Paralelo,
  input  B2,
  input  B1,
  input  B0
);

  wire and_1_out, and_2_out, and_3_out, and_4_out, and_5_out, and_6_out, clock_1_out, clock_2_out,
       j_k_ff_1_q, j_k_ff_2_q, j_k_ff_3_q, j_k_ff_4_q, j_k_ff_5_q, j_k_ff_6_q;

  Clock clock_1 (.out(clock_1_out));
  Clock clock_2 (.out(clock_2_out));
  and and_1 (and_1_out, Carreg__Paralelo, B2);
  LED led_1 (.in(j_k_ff_1_q));
  J_K_Flip_Flop j_k_ff_1 (
    .J(j_k_ff_3_q), .clk(clock_1_out), .K(j_k_ff_3_q), .Q(j_k_ff_1_q));  // open: Qn, preset, en, reset
  LED led_2 (.in(j_k_ff_2_q));
  J_K_Flip_Flop j_k_ff_2 (
    .J(j_k_ff_4_q), .clk(clock_2_out), .K(j_k_ff_4_q), .Q(j_k_ff_2_q), .preset(and_1_out), .reset(and_2_out));  // open: Qn, en
  and and_2 (and_2_out, Carreg__Paralelo, ~B2);  // AND_Gate
  LED led_3 (.in(j_k_ff_3_q));
  J_K_Flip_Flop j_k_ff_3 (.J(1'b1), .clk(clock_1_out), .K(1'b1), .Q(j_k_ff_3_q));  // open: Qn, preset, en, reset
  J_K_Flip_Flop j_k_ff_4 (
    .J(1'b1), .clk(clock_2_out), .K(1'b1), .Q(j_k_ff_4_q), .preset(and_4_out), .reset(and_3_out));  // open: Qn, en
  and and_3 (and_3_out, Carreg__Paralelo, ~B1);  // AND_Gate
  and and_4 (and_4_out, Carreg__Paralelo, B1);
  LED led_4 (.in(j_k_ff_4_q));
  and and_5 (and_5_out, Carreg__Paralelo, B0);
  LED led_5 (.in(j_k_ff_5_q));
  J_K_Flip_Flop j_k_ff_5 (
    .J(1'b0), .clk(clock_1_out), .K(1'b0), .Q(j_k_ff_5_q), .preset(escreve_1), .reset(escreve_0));  // open: Qn, en
  LED led_6 (.in(j_k_ff_6_q));
  J_K_Flip_Flop j_k_ff_6 (
    .J(1'b0), .clk(clock_2_out), .K(1'b0), .Q(j_k_ff_6_q), .preset(and_5_out), .reset(and_6_out));  // open: Qn, en
  and and_6 (and_6_out, Carreg__Paralelo, ~B0);  // AND_Gate

  // Notes on the sheet:
  //   contador de 2 ciclos (pares ou ímpares)
  //   O contador acima pode ser posto no ciclo par ou ímpar mediante a escrita de 0 ou 1 no bms.
  //   Observe que podem ser necessários alguns pulsos pra retornar ao estado inicial de cada ciclo.
  //   Contador de 2 ciclos (pares ou ímpares) (Carregamento paralelo).
  //   O contador acima pode ser posto em qualquer estado do ciclo par ou ímpar mediante o circuito de carregamento paralelo.
endmodule
