// Logisim project Exemplo_da_Aula_de_19_08_2021.circ as structural Verilog: 1 circuit, main circuit main
module main (
  input  in_1,
  input  in_2,
  input  in_3,
  output out_4,
  output out_5
);

  wire and_1_out, nand_1_out;

  and and_1 (and_1_out, in_1, in_2);
  or or_1 (out_5, and_1_out, ~in_3);  // OR_Gate
  nand nand_1 (nand_1_out, in_1, in_2);
  nand nand_2 (out_4, nand_1_out, in_3);
endmodule
