// Logisim project Forma_NAND_e_Forma_NOR.circ as structural Verilog: 1 circuit, main circuit main
module main (
  input  A,
  input  B,
  input  C
);

  wire and_1_out, and_2_out, and_3_out, and_4_out, and_5_out, nand_1_out, nand_2_out, nand_3_out, nand_4_out,
       nand_5_out, nand_6_out, nand_7_out, nand_8_out, nor_1_out, nor_2_out, nor_3_out, nor_4_out, nor_5_out,
       nor_6_out, nor_7_out, nor_8_out, not_1_out, not_2_out, not_3_out, or_1_out, or_2_out, or_3_out,
       or_4_out, or_5_out;

  not not_1 (not_1_out, A);
  not not_2 (not_2_out, C);
  not not_3 (not_3_out, B);
  and and_1 (and_1_out, not_1_out, B, not_2_out);
  and and_2 (and_2_out, not_1_out, B, C);
  and and_3 (and_3_out, A, not_3_out, C);
  and and_4 (and_4_out, A, B, C);
  nand nand_1 (nand_1_out, not_1_out, B, not_2_out);
  nand nand_2 (nand_2_out, not_1_out, B, C);
  nand nand_3 (nand_3_out, A, not_3_out, C);
  nand nand_4 (nand_4_out, A, B, C);
  nand nand_5 (nand_5_out, not_1_out, B);
  nand nand_6 (nand_6_out, A, C);
  or or_1 (or_1_out, A, B, C);
  or or_2 (or_2_out, A, B, not_2_out);
  or or_3 (or_3_out, not_1_out, B, C);
  or or_4 (or_4_out, not_1_out, not_3_out, C);
  nor nor_1 (nor_1_out, A, B, C);
  nor nor_2 (nor_2_out, A, B, not_2_out);
  nor nor_3 (nor_3_out, not_1_out, B, C);
  nor nor_4 (nor_4_out, not_1_out, not_3_out, C);
  nor nor_5 (nor_5_out, A, B);
  nor nor_6 (nor_6_out, not_1_out, C);
  or or_5 (or_5_out, and_1_out, and_2_out, and_3_out, and_4_out);
  nand nand_7 (nand_7_out, nand_1_out, nand_2_out, nand_3_out, nand_4_out);
  nand nand_8 (nand_8_out, nand_5_out, nand_6_out);
  and and_5 (and_5_out, or_1_out, or_2_out, or_3_out, or_4_out);
  nor nor_7 (nor_7_out, nor_1_out, nor_2_out, nor_3_out, nor_4_out);
  LED led_1 (.in(nor_7_out));
  nor nor_8 (nor_8_out, nor_5_out, nor_6_out);
  LED led_2 (.in(nor_8_out));
  LED led_3 (.in(or_5_out));
  LED led_4 (.in(nand_7_out));
  LED led_5 (.in(nand_8_out));
  LED led_6 (.in(and_5_out));

  // Notes on the sheet:
  //   A`BC`
  //   A`BC
  //   AB`C
  //   ABC
  //   Nesse exemplo valem 1 os minitermos 2,3,5,7
  //   (1) Forma Canônica SdP
  //   (2) Forma NAND partindo da Canônica SdP
  //   (3) Forma NAND partindo da Forma Mínima
  //   (4) Forma Canônica PdS
  //   (5) Forma NOR partindo da Canônica PdS
  //   (6) Forma NOR partindo da PdS Simplificada
endmodule
