// Logisim project MUX_2_pra_1_de_2_bits_de_dados.circ as structural Verilog: 1 circuit, main circuit main
module main (
  input  A1,
  input  A0,
  input  B1,
  input  B0,
  input  CTRL
);

  wire and_1_out, and_2_out, and_3_out, and_4_out, or_1_out, or_2_out;

  and and_1 (and_1_out, A1, ~CTRL);  // AND_Gate
  and and_2 (and_2_out, A0, ~CTRL);  // AND_Gate
  and and_3 (and_3_out, B1, CTRL);
  and and_4 (and_4_out, B0, CTRL);
  or or_1 (or_1_out, and_1_out, and_3_out);
  or or_2 (or_2_out, and_2_out, and_4_out);
  LED led_1 (.in(or_1_out));
  LED led_2 (.in(or_2_out));

  // Notes on the sheet:
  //   MUX 2 :1 de 2 bits de dados
  //   S1
  //   S0
endmodule
