// Logisim project MUX_BLU_exemplos_aula_06_11_2020.circ as structural Verilog: 1 circuit, main circuit main
module main (
  input  A,
  input  B,
  input  A_2,
  input  B_2,
  input  C,
  input  C_2,
  input  D,
  input  A_3,
  input  B_3,
  input  C_3,
  input  D_2
);

  wire and_1_out, multiplexer_1_out, multiplexer_2_out, multiplexer_3_out, not_1_out, not_2_out, xnor_1_out;

  not not_1 (not_1_out, C);
  not not_2 (not_2_out, D_2);
  Multiplexer #(.select(2), .enable("false")) multiplexer_1 (
    .in0(not_1_out), .in1(C), .in2(1'b0), .in3(not_1_out), .out(multiplexer_1_out), .sel({A, B}));
  LED led_1 (.in(multiplexer_1_out));
  Multiplexer #(.select(3), .enable("false")) multiplexer_2 (
    .in0(not_2_out), .in1(D_2), .in2(1'b0), .in3(not_2_out), .in4(1'b0), .in5(1'b0), .in6(1'b0), .in7(1'b0),
    .out(multiplexer_2_out), .sel({A_3, B_3, C_3}));
  LED led_2 (.in(multiplexer_2_out));
  and and_1 (and_1_out, C_2, ~D);  // AND_Gate
  xnor xnor_1 (xnor_1_out, C_2, D);
  Multiplexer #(.select(2), .enable("false")) multiplexer_3 (
    .in0(xnor_1_out), .in1(and_1_out), .in2(1'b0), .in3(1'b0), .out(multiplexer_3_out), .sel({A_2, B_2}));
  LED led_3 (.in(multiplexer_3_out));

  // Notes on the sheet:
  //   F(A,B,C) = minitermos (0,3,6) no MUX 4 :1 de um bit de dados  
  //   F(A,B,C,D) = minitermos (0,3,6) no MUX 8 :1 de um bit de dados  
  //   F(A,B,C,D) = minitermos (0,3,6) no MUX 4 :1 de um bit de dados  
endmodule
