// Logisim project MUX_and_decododer_4_to_1_19_08_2021.circ as structural Verilog: 1 circuit, main circuit main
module main (
  input  X,
  input  Y,
  input  Z,
  input  W,
  input  C1,
  input  C0,
  input  C1_2,
  input  C0_2,
  output ZERO,
  output UM,
  output S,
  output DOIS,
  output TRES
);

  wire and_1_out, and_2_out, and_3_out, and_4_out;

  and and_1 (and_1_out, X, ~C1_2, ~C0_2);  // AND_Gate
  and and_2 (and_2_out, Y, ~C1_2, C0_2);  // AND_Gate
  and and_3 (and_3_out, Z, C1_2, ~C0_2);  // AND_Gate
  and and_4 (and_4_out, W, C1_2, C0_2);
  or or_1 (S, and_1_out, and_2_out, and_3_out, and_4_out);
  and and_5 (ZERO, 1'b1, ~C1, ~C0);  // AND_Gate
  and and_6 (UM, 1'b1, ~C1, C0);  // AND_Gate
  and and_7 (DOIS, 1'b1, C1, ~C0);  // AND_Gate
  and and_8 (TRES, 1'b1, C1, C0);
endmodule
