// Logisim project Somador_Completo_1bit.circ as structural Verilog: 1 circuit, main circuit main
module main (
  input  Cin,
  input  A,
  input  B,
  output Sum,
  output out_5
);

  wire and_1_out, and_2_out, xor_1_out;

  and and_1 (and_1_out, A, B);
  xor xor_1 (xor_1_out, A, B);
  or or_1 (out_5, and_1_out, and_2_out);
  and and_2 (and_2_out, xor_1_out, Cin);
  xor xor_2 (Sum, Cin, xor_1_out);

  // Notes on the sheet:
  //   COut
endmodule
