// Logisim project Somador_Subtrator_4bits.circ as structural Verilog: 1 circuit, main circuit main
module main (
  input  A3,
  input  A2,
  input  A1,
  input  A0,
  input  B3,
  input  B2,
  input  B1,
  input  B0,
  input  SUB_nADD
);

  wire C1_B_o0, C1_B_o1, C1_B_o2, C1_B_o3, main_1_out_5, main_1_sum, main_2_out_5, main_2_sum,
       Somador_Completo_de_1_bit_2_out_5, Somador_Completo_de_1_bit_2_sum, Somador_Completo_de_1_bit_out_5,
       Somador_Completo_de_1_bit_sum, xor_1_out;

  LED Overflow_Sem_Sinal (.in(Somador_Completo_de_1_bit_out_5));
  xor xor_1 (xor_1_out, Somador_Completo_de_1_bit_out_5, main_1_out_5);
  LED Overflow_para_C2 (.in(xor_1_out));
  Somador_Completo_1bit_main Somador_Completo_de_1_bit (
    .A(A3), .B(C1_B_o3), .Sum(Somador_Completo_de_1_bit_sum), .Cin(main_1_out_5),
    .out_5(Somador_Completo_de_1_bit_out_5));
  LED S3 (.in(Somador_Completo_de_1_bit_sum));
  Somador_Completo_1bit_main main_1 (.A(A2), .B(C1_B_o2), .Sum(main_1_sum), .Cin(main_2_out_5), .out_5(main_1_out_5));
  LED S2 (.in(main_1_sum));
  LED S1 (.in(main_2_sum));
  Somador_Completo_1bit_main main_2 (
    .A(A1), .B(C1_B_o1), .Sum(main_2_sum), .Cin(Somador_Completo_de_1_bit_2_out_5), .out_5(main_2_out_5));
  Somador_Completo_1bit_main Somador_Completo_de_1_bit_2 (
    .A(A0), .B(C1_B_o0), .Sum(Somador_Completo_de_1_bit_2_sum), .Cin(SUB_nADD),
    .out_5(Somador_Completo_de_1_bit_2_out_5));
  LED S0 (.in(Somador_Completo_de_1_bit_2_sum));
  Complemento_de_1_com_crtl_main C1_B (
    .ctrl(SUB_nADD), .e3(B3), .e2(B2), .e1(B1), .e0(B0), .o3(C1_B_o3), .o2(C1_B_o2), .o1(C1_B_o1),
    .o0(C1_B_o0));

  // Notes on the sheet:
  //   Somador-Subtrator de 4 bits
endmodule
