// Logisim project contador_cresc_decres.circ as structural Verilog: 1 circuit, main circuit main
module main (
  input  ctrl__cresc___0__ou_decresc___1,
  input  ctrl__cresc___0__ou_decresc___1_2,
  input  Carreg__Paralelo,
  input  B2,
  input  B1,
  input  B0
);

  wire and_1_out, and_2_out, and_3_out, and_4_out, and_5_out, and_6_out, and_7_out, and_8_out, and_9_out,
       and_10_out, and_11_out, and_12_out, clock_1_out, clock_2_out, clock_3_out, clock_4_out, j_k_ff_1_q,
       j_k_ff_2_q, j_k_ff_3_q, j_k_ff_4_q, j_k_ff_4_qn, j_k_ff_5_q, j_k_ff_6_q, j_k_ff_7_q, j_k_ff_8_q,
       j_k_ff_8_qn, j_k_ff_9_q, j_k_ff_9_qn, j_k_ff_10_q, j_k_ff_10_qn, j_k_ff_11_q, j_k_ff_11_qn,
       j_k_ff_12_q, j_k_ff_12_qn, multiplexer_1_out, multiplexer_2_out, multiplexer_3_out, multiplexer_4_out;

  Clock clock_1 (.out(clock_1_out));
  Clock clock_2 (.out(clock_2_out));
  and and_1 (and_1_out, j_k_ff_3_q, j_k_ff_7_q);
  and and_2 (and_2_out, j_k_ff_8_qn, j_k_ff_4_qn);
  Clock clock_3 (.out(clock_3_out));
  Multiplexer #(.enable("false")) multiplexer_1 (
    .in0(and_3_out), .in1(and_4_out), .out(multiplexer_1_out), .sel(ctrl__cresc___0__ou_decresc___1));
  Clock clock_4 (.out(clock_4_out));
  Multiplexer #(.enable("false")) multiplexer_2 (
    .in0(and_5_out), .in1(and_6_out), .out(multiplexer_2_out), .sel(ctrl__cresc___0__ou_decresc___1_2));
  LED led_1 (.in(j_k_ff_1_q));
  J_K_Flip_Flop j_k_ff_1 (
    .J(and_1_out), .clk(clock_1_out), .K(and_1_out), .Q(j_k_ff_1_q));  // open: Qn, preset, en, reset
  LED led_2 (.in(j_k_ff_2_q));
  J_K_Flip_Flop j_k_ff_2 (
    .J(and_2_out), .clk(clock_2_out), .K(and_2_out), .Q(j_k_ff_2_q));  // open: Qn, preset, en, reset
  and and_3 (and_3_out, j_k_ff_9_q, j_k_ff_11_q);
  and and_4 (and_4_out, j_k_ff_11_qn, j_k_ff_9_qn);
  and and_5 (and_5_out, j_k_ff_10_q, j_k_ff_12_q);
  and and_6 (and_6_out, j_k_ff_12_qn, j_k_ff_10_qn);
  and and_7 (and_7_out, Carreg__Paralelo, B2);
  LED led_3 (.in(j_k_ff_3_q));
  J_K_Flip_Flop j_k_ff_3 (
    .J(j_k_ff_7_q), .clk(clock_1_out), .K(j_k_ff_7_q), .Q(j_k_ff_3_q));  // open: Qn, preset, en, reset
  LED led_4 (.in(j_k_ff_4_q));
  J_K_Flip_Flop j_k_ff_4 (
    .J(j_k_ff_8_qn), .clk(clock_2_out), .K(j_k_ff_8_qn), .Q(j_k_ff_4_q), .Qn(j_k_ff_4_qn));  // open: preset, en, reset
  LED led_5 (.in(j_k_ff_5_q));
  J_K_Flip_Flop j_k_ff_5 (
    .J(multiplexer_1_out), .clk(clock_3_out), .K(multiplexer_1_out), .Q(j_k_ff_5_q));  // open: Qn, preset, en, reset
  LED led_6 (.in(j_k_ff_6_q));
  J_K_Flip_Flop j_k_ff_6 (
    .J(multiplexer_2_out), .clk(clock_4_out), .K(multiplexer_2_out), .Q(j_k_ff_6_q), .preset(and_7_out),
    .reset(and_8_out));  // open: Qn, en
  and and_8 (and_8_out, Carreg__Paralelo, ~B2);  // AND_Gate
  Multiplexer #(.enable("false")) multiplexer_3 (
    .in0(j_k_ff_11_q), .in1(j_k_ff_11_qn), .out(multiplexer_3_out), .sel(ctrl__cresc___0__ou_decresc___1));
  Multiplexer #(.enable("false")) multiplexer_4 (
    .in0(j_k_ff_12_q), .in1(j_k_ff_12_qn), .out(multiplexer_4_out), .sel(ctrl__cresc___0__ou_decresc___1_2));
  and and_9 (and_9_out, Carreg__Paralelo, B1);
  LED led_7 (.in(j_k_ff_7_q));
  J_K_Flip_Flop j_k_ff_7 (.J(1'b1), .clk(clock_1_out), .K(1'b1), .Q(j_k_ff_7_q));  // open: Qn, preset, en, reset
  LED led_8 (.in(j_k_ff_8_q));
  J_K_Flip_Flop j_k_ff_8 (
    .J(1'b1), .clk(clock_2_out), .K(1'b1), .Q(j_k_ff_8_q), .Qn(j_k_ff_8_qn));  // open: preset, en, reset
  LED led_9 (.in(j_k_ff_9_q));
  J_K_Flip_Flop j_k_ff_9 (
    .J(multiplexer_3_out), .clk(clock_3_out), .K(multiplexer_3_out), .Q(j_k_ff_9_q), .Qn(j_k_ff_9_qn));  // open: preset, en, reset
  LED led_10 (.in(j_k_ff_10_q));
  J_K_Flip_Flop j_k_ff_10 (
    .J(multiplexer_4_out), .clk(clock_4_out), .K(multiplexer_4_out), .Q(j_k_ff_10_q), .Qn(j_k_ff_10_qn),
    .preset(and_9_out), .reset(and_10_out));  // open: en
  and and_10 (and_10_out, Carreg__Paralelo, ~B1);  // AND_Gate
  J_K_Flip_Flop j_k_ff_11 (
    .J(1'b1), .clk(clock_3_out), .K(1'b1), .Q(j_k_ff_11_q), .Qn(j_k_ff_11_qn));  // open: preset, en, reset
  J_K_Flip_Flop j_k_ff_12 (
    .J(1'b1), .clk(clock_4_out), .K(1'b1), .Q(j_k_ff_12_q), .Qn(j_k_ff_12_qn), .preset(and_11_out),
    .reset(and_12_out));  // open: en
  and and_11 (and_11_out, Carreg__Paralelo, B0);
  and and_12 (and_12_out, Carreg__Paralelo, ~B0);  // AND_Gate
  LED led_11 (.in(j_k_ff_11_q));
  LED led_12 (.in(j_k_ff_12_q));

  // Notes on the sheet:
  //   Crescente
  //   Decrescente
  //   Crescente-Decrescente
  //   Crescente-Decrescente. (Carregamento Paralelo.)
endmodule
