// Logisim project contador_gray_mod_6.circ as structural Verilog: 1 circuit, main circuit main
module main (
);

  wire and_1_out, and_2_out, clock_1_out, j_k_ff_1_q, j_k_ff_2_q, j_k_ff_2_qn, j_k_ff_3_q, j_k_ff_3_qn,
       or_1_out;

  Clock clock_1 (.out(clock_1_out));
  and and_1 (and_1_out, j_k_ff_2_q, j_k_ff_3_qn);
  LED led_1 (.in(j_k_ff_1_q));
  J_K_Flip_Flop j_k_ff_1 (
    .J(and_1_out), .clk(clock_1_out), .K(j_k_ff_3_q), .Q(j_k_ff_1_q));  // open: Qn, preset, en, reset
  and and_2 (and_2_out, j_k_ff_1_q, j_k_ff_3_q);
  J_K_Flip_Flop j_k_ff_2 (
    .J(j_k_ff_3_q), .clk(clock_1_out), .K(and_2_out), .Q(j_k_ff_2_q), .Qn(j_k_ff_2_qn));  // open: preset, en, reset
  LED led_2 (.in(j_k_ff_2_q));
  or or_1 (or_1_out, j_k_ff_1_q, j_k_ff_2_qn);
  LED led_3 (.in(j_k_ff_3_q));
  J_K_Flip_Flop j_k_ff_3 (
    .J(or_1_out), .clk(clock_1_out), .K(j_k_ff_2_q), .Q(j_k_ff_3_q), .Qn(j_k_ff_3_qn));  // open: preset, en, reset
endmodule
