// Logisim project mux_4_1.circ as structural Verilog: 2 circuits, main circuit main
module main (
  input  D0,
  input  D1,
  input  D2,
  input  D3,
  input  C0,
  input  C1
);

  wire and_1_out, and_2_out, and_3_out, and_4_out, or_1_out;

  and and_1 (and_1_out, D0, ~C0, ~C1);  // AND_Gate
  and and_2 (and_2_out, D1, ~C0, C1);  // AND_Gate
  and and_3 (and_3_out, D2, C0, ~C1);  // AND_Gate
  and and_4 (and_4_out, D3, C0, C1);
  LED led_1 (.in(and_1_out));
  LED led_2 (.in(and_2_out));
  LED led_3 (.in(and_3_out));
  LED led_4 (.in(and_4_out));
  or or_1 (or_1_out, and_1_out, and_2_out, and_3_out, and_4_out);
  // Probe on or_1_out

  // Notes on the sheet:
  //   MUX 4:1 DE 1 BIT
endmodule

module MUX_2BITS (
  input  D00,
  input  D10,
  input  D20,
  input  D30,
  input  D01,
  input  D11,
  input  D21,
  input  D31,
  input  C0,
  input  C1
);

  wire and_1_out, and_2_out, and_3_out, and_4_out, and_6_out, and_7_out, and_8_out, and_9_out, or_1_out,
       or_2_out;

  and and_1 (and_1_out, D00, ~C0, ~C1);  // AND_Gate
  and and_2 (and_2_out, D10, ~C0, C1);  // AND_Gate
  and and_3 (and_3_out, D20, C0, ~C1);  // AND_Gate
  and and_4 (and_4_out, D30, C0, C1);
  and and_5 (and_4_out, D30, C0, C1);
  and and_6 (and_6_out, D01, ~C0, ~C1);  // AND_Gate
  and and_7 (and_7_out, D11, ~C0, C1);  // AND_Gate
  and and_8 (and_8_out, D21, C0, ~C1);  // AND_Gate
  and and_9 (and_9_out, D31, C0, C1);
  and and_10 (and_9_out, D31, C0, C1);
  LED led_1 (.in(and_2_out));
  LED led_2 (.in(and_3_out));
  LED led_3 (.in(and_3_out));
  LED led_4 (.in(and_7_out));
  LED led_5 (.in(and_8_out));
  LED led_6 (.in(and_8_out));
  LED led_7 (.in(and_1_out));
  LED led_8 (.in(and_4_out));
  LED led_9 (.in(and_6_out));
  LED led_10 (.in(and_9_out));
  or or_1 (or_1_out, and_1_out, and_2_out, and_3_out, and_4_out);
  or or_2 (or_2_out, and_6_out, and_7_out, and_8_out, and_9_out);
  // Probe on or_1_out
  // Probe on or_2_out

  // Notes on the sheet:
  //   MUX 4:1 DE 2 BITS
endmodule
