// Logisim project mux_mult_saida.circ as structural Verilog: 1 circuit, main circuit main
module main (
  input  D0,
  input  D1,
  input  D2,
  input  D3,
  input  C0,
  input  C1,
  input  [1:0] in_7,
  input  [1:0] in_8,
  input  [1:0] in_9,
  input  [1:0] in_10,
  input  [1:0] in_11
);

  wire and_1_out, and_2_out, and_3_out, and_4_out, or_1_out;
  wire [1:0] demultiplexer_1_out0, demultiplexer_1_out1, demultiplexer_1_out2, demultiplexer_1_out3,
       multiplexer_1_out;

  and and_1 (and_1_out, D0, ~C0, ~C1);  // AND_Gate
  and and_2 (and_2_out, D1, ~C0, C1);  // AND_Gate
  and and_3 (and_3_out, D2, C0, ~C1);  // AND_Gate
  and and_4 (and_4_out, D3, C0, C1);
  LED led_1 (.in(and_1_out));
  LED led_2 (.in(and_2_out));
  LED led_3 (.in(and_3_out));
  LED led_4 (.in(and_4_out));
  Multiplexer #(.select(2), .width(2)) multiplexer_1 (
    .in0(in_7), .in1(in_8), .in2(in_9), .in3(in_10), .out(multiplexer_1_out), .sel(in_11));
  // Probe on multiplexer_1_out
  Demultiplexer #(.select(2), .width(2)) demultiplexer_1 (
    .out0(demultiplexer_1_out0), .out1(demultiplexer_1_out1), .out2(demultiplexer_1_out2),
    .out3(demultiplexer_1_out3), .in(multiplexer_1_out), .sel(in_11));
  // Probe on demultiplexer_1_out0
  // Probe on demultiplexer_1_out1
  // Probe on demultiplexer_1_out2
  // Probe on demultiplexer_1_out3
  or or_1 (or_1_out, and_1_out, and_2_out, and_3_out, and_4_out);
  // Probe on or_1_out

  // Notes on the sheet:
  //   MUX 4:1 DE 1 BIT
endmodule
