// Logisim project registrador_2bits.circ as structural Verilog: 2 circuits, main circuit main
module main (
  input  in_1,
  input  EDE,
  input  EDD,
  input  in_4,
  input  in_5,
  input  [3:0] in_6,
  output SaidaD
);

  wire clock_1_out, controlled_buffer_1_out, controlled_buffer_2_out, controlled_buffer_3_out,
       controlled_buffer_4_out, d_ff_1_q, d_ff_2_q, d_ff_3_q, multiplexer_1_out, multiplexer_2_out,
       multiplexer_3_out, multiplexer_4_out;

  Clock clock_1 (.out(clock_1_out));
  Multiplexer #(.select(2)) multiplexer_1 (
    .in0(d_ff_1_q), .in1(EDD), .in2(d_ff_2_q), .in3(in_6[3]), .out(multiplexer_1_out), .sel({in_4, in_5}));
  D_Flip_Flop d_ff_1 (.D(multiplexer_1_out), .clk(clock_1_out), .Q(d_ff_1_q));  // open: Qn, preset, reset
  assign controlled_buffer_1_out = in_1 ? d_ff_1_q : 1'bz;  // Controlled_Buffer controlled_buffer_1
  LED led_1 (.in(controlled_buffer_1_out));
  D_Flip_Flop d_ff_2 (.D(multiplexer_2_out), .clk(clock_1_out), .Q(d_ff_2_q));  // open: Qn, preset, reset
  Multiplexer #(.select(2)) multiplexer_2 (
    .in0(d_ff_2_q), .in1(d_ff_1_q), .in2(d_ff_3_q), .in3(in_6[2]), .out(multiplexer_2_out), .sel({in_4, in_5}));
  assign controlled_buffer_2_out = in_1 ? d_ff_2_q : 1'bz;  // Controlled_Buffer controlled_buffer_2
  LED led_2 (.in(controlled_buffer_2_out));
  Multiplexer #(.select(2)) multiplexer_3 (
    .in0(d_ff_3_q), .in1(d_ff_2_q), .in2(SaidaD), .in3(in_6[1]), .out(multiplexer_3_out), .sel({in_4, in_5}));
  D_Flip_Flop d_ff_3 (.D(multiplexer_3_out), .clk(clock_1_out), .Q(d_ff_3_q));  // open: Qn, preset, reset
  assign controlled_buffer_3_out = in_1 ? d_ff_3_q : 1'bz;  // Controlled_Buffer controlled_buffer_3
  LED led_3 (.in(controlled_buffer_3_out));
  D_Flip_Flop d_ff_4 (.D(multiplexer_4_out), .clk(clock_1_out), .Q(SaidaD));  // open: Qn, preset, reset
  Multiplexer #(.select(2)) multiplexer_4 (
    .in0(SaidaD), .in1(d_ff_3_q), .in2(EDE), .in3(in_6[0]), .out(multiplexer_4_out), .sel({in_4, in_5}));
  assign controlled_buffer_4_out = in_1 ? SaidaD : 1'bz;  // Controlled_Buffer controlled_buffer_4
  LED led_4 (.in(controlled_buffer_4_out));

  // Other names for the same wires on the sheet: LER = in_1

  // Notes on the sheet:
  //   MANTEM O ESTADO - CONTROLE 0
  //   EDD - CONTROLE 1
  //   EDE - CONTROLE 2
  //   ARMAZENAR - CONTROLE 3
endmodule

module bits_2 (
  input  LER,
  input  EDE,
  input  EDD,
  input  in_4,
  input  in_5,
  input  c1,
  input  c0,
  input  [1:0] dados
);

  wire clk_out, controlled_buffer_1_out, controlled_buffer_2_out, d_ff_1_q, d_ff_2_q, multiplexer_1_out,
       multiplexer_2_out;

  Clock clk (.out(clk_out));
  Multiplexer #(.select(2)) multiplexer_1 (
    .in0(d_ff_1_q), .in1(EDD), .in2(d_ff_2_q), .in3(dados[1]), .out(multiplexer_1_out), .sel({c1, c0}));
  LED led_1 (.in(controlled_buffer_1_out));
  assign controlled_buffer_1_out = LER ? d_ff_1_q : 1'bz;  // Controlled_Buffer controlled_buffer_1
  D_Flip_Flop d_ff_1 (.D(multiplexer_1_out), .clk(clk_out), .Q(d_ff_1_q), .reset(in_4));  // open: Qn, preset
  Multiplexer #(.select(2)) multiplexer_2 (
    .in0(d_ff_2_q), .in1(d_ff_1_q), .in2(EDE), .in3(dados[0]), .out(multiplexer_2_out), .sel({c1, c0}));
  D_Flip_Flop d_ff_2 (.D(multiplexer_2_out), .clk(clk_out), .Q(d_ff_2_q), .reset(in_5));  // open: Qn, preset
  LED led_2 (.in(controlled_buffer_2_out));
  assign controlled_buffer_2_out = LER ? d_ff_2_q : 1'bz;  // Controlled_Buffer controlled_buffer_2
  // Probe on d_ff_2_q

  // Notes on the sheet:
  //   EDE - direita → esquerda
  //   EDD - esquerda → direita
endmodule
