// Logisim project registrador_3_4_5bits.circ as structural Verilog: 3 circuits, main circuit main
module main (
  input  LER,
  input  EDE,
  input  EDD,
  input  c1,
  input  c0,
  input  [2:0] in_6,
  output b_Ms,
  output bms
);

  wire clock_1_out, controlled_buffer_1_out, controlled_buffer_2_out, controlled_buffer_3_out, d_ff_2_q,
       multiplexer_1_out, multiplexer_2_out, multiplexer_3_out;

  Clock clock_1 (.out(clock_1_out));
  Multiplexer #(.select(2)) multiplexer_1 (
    .in0(b_Ms), .in1(EDD), .in2(d_ff_2_q), .in3(in_6[2]), .out(multiplexer_1_out), .sel({c1, c0}));
  D_Flip_Flop d_ff_1 (.D(multiplexer_1_out), .clk(clock_1_out), .Q(b_Ms));  // open: Qn, preset, reset
  LED led_1 (.in(controlled_buffer_1_out));
  assign controlled_buffer_1_out = LER ? b_Ms : 1'bz;  // Controlled_Buffer controlled_buffer_1
  Multiplexer #(.select(2)) multiplexer_2 (
    .in0(d_ff_2_q), .in1(b_Ms), .in2(bms), .in3(in_6[1]), .out(multiplexer_2_out), .sel({c1, c0}));
  D_Flip_Flop d_ff_2 (.D(multiplexer_2_out), .clk(clock_1_out), .Q(d_ff_2_q));  // open: Qn, preset, reset
  LED led_2 (.in(controlled_buffer_2_out));
  assign controlled_buffer_2_out = LER ? d_ff_2_q : 1'bz;  // Controlled_Buffer controlled_buffer_2
  D_Flip_Flop d_ff_3 (.D(multiplexer_3_out), .clk(clock_1_out), .Q(bms));  // open: Qn, preset, reset
  Multiplexer #(.select(2)) multiplexer_3 (
    .in0(bms), .in1(d_ff_2_q), .in2(EDE), .in3(in_6[0]), .out(multiplexer_3_out), .sel({c1, c0}));
  LED led_3 (.in(controlled_buffer_3_out));
  assign controlled_buffer_3_out = LER ? bms : 1'bz;  // Controlled_Buffer controlled_buffer_3

  // Notes on the sheet:
  //   EDE - direita → esquerda
  //   EDD - esquerda → direita
endmodule

module bits_4 (
  input  LER,
  input  EDE,
  input  EDD,
  input  in_4,
  input  in_5,
  input  [3:0] in_6,
  output bMs,
  output b_ms
);

  wire clock_1_out, controlled_buffer_1_out, controlled_buffer_2_out, controlled_buffer_3_out,
       controlled_buffer_4_out, d_ff_2_q, d_ff_3_q, multiplexer_1_out, multiplexer_2_out, multiplexer_3_out,
       multiplexer_4_out;

  Clock clock_1 (.out(clock_1_out));
  D_Flip_Flop d_ff_1 (.D(multiplexer_1_out), .clk(clock_1_out), .Q(bMs));  // open: Qn, preset, reset
  Multiplexer #(.select(2)) multiplexer_1 (
    .in0(bMs), .in1(EDD), .in2(d_ff_2_q), .in3(in_6[3]), .out(multiplexer_1_out), .sel({in_4, in_5}));
  LED led_1 (.in(controlled_buffer_1_out));
  assign controlled_buffer_1_out = LER ? bMs : 1'bz;  // Controlled_Buffer controlled_buffer_1
  Multiplexer #(.select(2)) multiplexer_2 (
    .in0(d_ff_2_q), .in1(bMs), .in2(d_ff_3_q), .in3(in_6[2]), .out(multiplexer_2_out), .sel({in_4, in_5}));
  D_Flip_Flop d_ff_2 (.D(multiplexer_2_out), .clk(clock_1_out), .Q(d_ff_2_q));  // open: Qn, preset, reset
  LED led_2 (.in(controlled_buffer_2_out));
  assign controlled_buffer_2_out = LER ? d_ff_2_q : 1'bz;  // Controlled_Buffer controlled_buffer_2
  D_Flip_Flop d_ff_3 (.D(multiplexer_3_out), .clk(clock_1_out), .Q(d_ff_3_q));  // open: Qn, preset, reset
  Multiplexer #(.select(2)) multiplexer_3 (
    .in0(d_ff_3_q), .in1(d_ff_2_q), .in2(b_ms), .in3(in_6[1]), .out(multiplexer_3_out), .sel({in_4, in_5}));
  LED led_3 (.in(controlled_buffer_3_out));
  assign controlled_buffer_3_out = LER ? d_ff_3_q : 1'bz;  // Controlled_Buffer controlled_buffer_3
  Multiplexer #(.select(2)) multiplexer_4 (
    .in0(b_ms), .in1(d_ff_3_q), .in2(EDE), .in3(in_6[0]), .out(multiplexer_4_out), .sel({in_4, in_5}));
  D_Flip_Flop d_ff_4 (.D(multiplexer_4_out), .clk(clock_1_out), .Q(b_ms));  // open: Qn, preset, reset
  LED led_4 (.in(controlled_buffer_4_out));
  assign controlled_buffer_4_out = LER ? b_ms : 1'bz;  // Controlled_Buffer controlled_buffer_4

  // Other names for the same wires on the sheet: b0 = in_6[0]; b1 = in_6[1]; b2 = in_6[2]; b3 = in_6[3]

  // Notes on the sheet:
  //   EDD - esquerda → direita
  //   EDE - direita → esquerda
endmodule

module bits_5 (
  input  LER,
  input  EDE,
  input  EDD,
  input  in_4,
  input  in_5,
  input  [4:0] in_6,
  output bMs,
  output b_ms
);

  wire clock_1_out, controlled_buffer_1_out, controlled_buffer_2_out, controlled_buffer_3_out,
       controlled_buffer_4_out, controlled_buffer_5_out, d_ff_2_q, d_ff_3_q, d_ff_4_q, multiplexer_1_out,
       multiplexer_2_out, multiplexer_3_out, multiplexer_4_out, multiplexer_5_out;

  Clock clock_1 (.out(clock_1_out));
  Multiplexer #(.select(2)) multiplexer_1 (
    .in0(bMs), .in1(EDD), .in2(d_ff_2_q), .in3(in_6[4]), .out(multiplexer_1_out), .sel({in_4, in_5}));
  D_Flip_Flop d_ff_1 (.D(multiplexer_1_out), .clk(clock_1_out), .Q(bMs));  // open: Qn, preset, reset
  LED led_1 (.in(controlled_buffer_1_out));
  assign controlled_buffer_1_out = LER ? bMs : 1'bz;  // Controlled_Buffer controlled_buffer_1
  D_Flip_Flop d_ff_2 (.D(multiplexer_2_out), .clk(clock_1_out), .Q(d_ff_2_q));  // open: Qn, preset, reset
  Multiplexer #(.select(2)) multiplexer_2 (
    .in0(d_ff_2_q), .in1(bMs), .in2(d_ff_3_q), .in3(in_6[3]), .out(multiplexer_2_out), .sel({in_4, in_5}));
  LED led_2 (.in(controlled_buffer_2_out));
  assign controlled_buffer_2_out = LER ? d_ff_2_q : 1'bz;  // Controlled_Buffer controlled_buffer_2
  D_Flip_Flop d_ff_3 (.D(multiplexer_3_out), .clk(clock_1_out), .Q(d_ff_3_q));  // open: Qn, preset, reset
  Multiplexer #(.select(2)) multiplexer_3 (
    .in0(d_ff_3_q), .in1(d_ff_2_q), .in2(d_ff_4_q), .in3(in_6[2]), .out(multiplexer_3_out), .sel({in_4, in_5}));
  LED led_3 (.in(controlled_buffer_3_out));
  assign controlled_buffer_3_out = LER ? d_ff_3_q : 1'bz;  // Controlled_Buffer controlled_buffer_3
  Multiplexer #(.select(2)) multiplexer_4 (
    .in0(d_ff_4_q), .in1(d_ff_3_q), .in2(b_ms), .in3(in_6[1]), .out(multiplexer_4_out), .sel({in_4, in_5}));
  D_Flip_Flop d_ff_4 (.D(multiplexer_4_out), .clk(clock_1_out), .Q(d_ff_4_q));  // open: Qn, preset, reset
  LED led_4 (.in(controlled_buffer_4_out));
  assign controlled_buffer_4_out = LER ? d_ff_4_q : 1'bz;  // Controlled_Buffer controlled_buffer_4
  D_Flip_Flop d_ff_5 (.D(multiplexer_5_out), .clk(clock_1_out), .Q(b_ms));  // open: Qn, preset, reset
  Multiplexer #(.select(2)) multiplexer_5 (
    .in0(b_ms), .in1(d_ff_4_q), .in2(EDE), .in3(in_6[0]), .out(multiplexer_5_out), .sel({in_4, in_5}));
  LED led_5 (.in(controlled_buffer_5_out));
  assign controlled_buffer_5_out = LER ? b_ms : 1'bz;  // Controlled_Buffer controlled_buffer_5

  // Other names for the same wires on the sheet: b0 = in_6[0]; b1 = in_6[1]; b2 = in_6[2]; b3 = in_6[3]; b4 = in_6[4]

  // Notes on the sheet:
  //   EDD - esquerda → direita
  //   EDE - direita → esquerda
endmodule
