// Logisim project registrador_Deslocamento.circ as structural Verilog: 1 circuit, main circuit main
module main (
  input  in_1,
  input  FF_D,
  output out_3,
  output out_4,
  output out_5,
  output out_6,
  output out_7,
  output out_8,
  output out_9,
  output out_10
);

  wire clock_1_out, clock_2_out, j_k_ff_1_qn, j_k_ff_2_qn, j_k_ff_3_qn, not_1_out;

  not not_1 (not_1_out, in_1);
  Clock clock_1 (.out(clock_1_out));
  Clock clock_2 (.out(clock_2_out));
  J_K_Flip_Flop #(.trigger("falling")) j_k_ff_1 (
    .J(in_1), .K(not_1_out), .clk(clock_1_out), .Q(out_3), .Qn(j_k_ff_1_qn));  // open: preset, reset
  D_Flip_Flop #(.trigger("falling")) d_ff_1 (.D(FF_D), .clk(clock_2_out), .Q(out_7));  // open: Qn, preset, reset
  J_K_Flip_Flop #(.trigger("falling")) j_k_ff_2 (
    .J(out_3), .K(j_k_ff_1_qn), .clk(clock_1_out), .Q(out_4), .Qn(j_k_ff_2_qn));  // open: preset, reset
  D_Flip_Flop #(.trigger("falling")) d_ff_2 (.D(out_7), .clk(clock_2_out), .Q(out_8));  // open: Qn, preset, reset
  J_K_Flip_Flop #(.trigger("falling")) j_k_ff_3 (
    .J(out_4), .K(j_k_ff_2_qn), .clk(clock_1_out), .Q(out_5), .Qn(j_k_ff_3_qn));  // open: preset, reset
  D_Flip_Flop #(.trigger("falling")) d_ff_3 (.D(out_8), .clk(clock_2_out), .Q(out_9));  // open: Qn, preset, reset
  J_K_Flip_Flop #(.trigger("falling")) j_k_ff_4 (
    .J(out_5), .K(j_k_ff_3_qn), .clk(clock_1_out), .Q(out_6));  // open: Qn, preset, reset
  D_Flip_Flop #(.trigger("falling")) d_ff_4 (.D(out_9), .clk(clock_2_out), .Q(out_10));  // open: Qn, preset, reset

  // Notes on the sheet:
  //   FF-JK
endmodule
