// Logisim project teste.circ as structural Verilog: 1 circuit, main circuit circuito_teste
module circuito_teste (
  input  A,
  input  B,
  input  A1,
  input  B1,
  input  in_5,
  input  in_6,
  input  in_7,
  input  in_8
);

  wire and_1_out, nand_1_out, nor_1_out, or_1_out;

  nand nand_1 (nand_1_out, A, B);
  or or_1 (or_1_out, ~A1, ~B1);  // OR_Gate
  nor nor_1 (nor_1_out, in_5, in_6);
  and and_1 (and_1_out, ~in_7, ~in_8);  // AND_Gate
  LED LED1 (.in(nand_1_out));
  LED led_1 (.in(or_1_out));
  LED led_2 (.in(nor_1_out));
  LED led_3 (.in(and_1_out));

  // Notes on the sheet:
  //   S= (A.B)'
  //   S=A'+B'
endmodule
